// Logisim project 01_basics.circ as structural Verilog: 9 circuits, main circuit main
module main (
);

  wire button_1_out, button_2_out, clkdiv8_1_clk_out, clock_1_out, display_01_1_dot, display_11_1_dot,
       display_11_1_sign;
  wire [3:0] display_01_1_hndrth, display_01_1_tenth, display_01_1_thousnth, display_01_1_zero,
       display_11_1_hndrth, display_11_1_tenth, display_11_1_thousnth, display_11_1_zero,
       display_hex_1_hihex, display_hex_1_lohex;
  wire [7:0] var8_1_count8_out;
  wire [15:0] display_11_1_level, graph_1_level_2, graph_1_level_3, graph_1_level_4, graph_1_level_5,
       graph_1_level_6, graph_1_level_7, graph_1_level_8, graph_1_level_9, graph_1_level_10,
       graph_1_level_11, graph_1_level_12, graph_1_level_13, graph_1_level_14, graph_1_level_15,
       graph_1_level_16, graph_1_level_17;

  Button button_1 (.out(button_1_out));
  Button button_2 (.out(button_2_out));
  VAR8 var8_1 (.INC(button_1_out), .DEC(button_2_out), .COUNT8_OUT(var8_1_count8_out));
  display_hex display_hex_1 (
    .D8_IN(var8_1_count8_out), .LOHEX(display_hex_1_lohex), .HIHEX(display_hex_1_hihex));  // open: LEVEL
  display_11 display_11_1 (
    .D8_IN(var8_1_count8_out), .LEVEL(display_11_1_level), .SIGN(display_11_1_sign),
    .ZERO(display_11_1_zero), .DOT(display_11_1_dot), .TENTH(display_11_1_tenth),
    .HNDRTH(display_11_1_hndrth), .THOUSNTH(display_11_1_thousnth));
  display_01 display_01_1 (
    .D8_IN(var8_1_count8_out), .ZERO(display_01_1_zero), .DOT(display_01_1_dot), .TENTH(display_01_1_tenth),
    .HNDRTH(display_01_1_hndrth), .THOUSNTH(display_01_1_thousnth));  // open: LEVEL
  Hex_Digit_Display hex_digit_display_1 (.value(display_hex_1_hihex));  // open: dp
  Hex_Digit_Display hex_digit_display_2 (.value(display_hex_1_lohex));  // open: dp
  _7_Segment_Display u_7_segment_display_1 (.g(display_11_1_sign));  // open: f, a, b, e, d, c, dp
  DotMatrix #(.matrixcols(3), .matrixrows(16)) dotmatrix_1 (
    .col0(display_11_1_level), .col1(display_11_1_level), .col2(display_11_1_level));
  Hex_Digit_Display hex_digit_display_3 (.value(display_11_1_zero), .dp(display_11_1_dot));
  Hex_Digit_Display hex_digit_display_4 (.value(display_01_1_zero), .dp(display_01_1_dot));
  Hex_Digit_Display hex_digit_display_5 (.value(display_11_1_tenth));  // open: dp
  Hex_Digit_Display hex_digit_display_6 (.value(display_11_1_hndrth));  // open: dp
  Hex_Digit_Display hex_digit_display_7 (.value(display_01_1_tenth));  // open: dp
  Hex_Digit_Display hex_digit_display_8 (.value(display_01_1_hndrth));  // open: dp
  Hex_Digit_Display hex_digit_display_9 (.value(display_11_1_thousnth));  // open: dp
  Hex_Digit_Display hex_digit_display_10 (.value(display_01_1_thousnth));  // open: dp
  Clock clock_1 (.out(clock_1_out));
  CLKDIV8 clkdiv8_1 (.CLK(clock_1_out), .DIV3(3'b100), .CLK_OUT(clkdiv8_1_clk_out));
  DotMatrix #(.matrixcols(1), .matrixrows(16)) dotmatrix_2 (.col0(graph_1_level_3));
  DotMatrix #(.matrixcols(1), .matrixrows(16)) dotmatrix_3 (.col0(graph_1_level_2));
  GRAPH graph_1 (
    .LEVEL(display_11_1_level), .CLK(clkdiv8_1_clk_out), .LEVEL_2(graph_1_level_2),
    .LEVEL_3(graph_1_level_3), .LEVEL_4(graph_1_level_4), .LEVEL_5(graph_1_level_5),
    .LEVEL_6(graph_1_level_6), .LEVEL_7(graph_1_level_7), .LEVEL_8(graph_1_level_8),
    .LEVEL_9(graph_1_level_9), .LEVEL_10(graph_1_level_10), .LEVEL_11(graph_1_level_11),
    .LEVEL_12(graph_1_level_12), .LEVEL_13(graph_1_level_13), .LEVEL_14(graph_1_level_14),
    .LEVEL_15(graph_1_level_15), .LEVEL_16(graph_1_level_16), .LEVEL_17(graph_1_level_17));
  DotMatrix #(.matrixcols(1), .matrixrows(16)) dotmatrix_4 (.col0(graph_1_level_7));
  DotMatrix #(.matrixcols(1), .matrixrows(16)) dotmatrix_5 (.col0(graph_1_level_10));
  DotMatrix #(.matrixcols(1), .matrixrows(16)) dotmatrix_6 (.col0(graph_1_level_11));
  DotMatrix #(.matrixcols(1), .matrixrows(16)) dotmatrix_7 (.col0(graph_1_level_4));
  DotMatrix #(.matrixcols(1), .matrixrows(16)) dotmatrix_8 (.col0(graph_1_level_9));
  DotMatrix #(.matrixcols(1), .matrixrows(16)) dotmatrix_9 (.col0(graph_1_level_6));
  DotMatrix #(.matrixcols(1), .matrixrows(16)) dotmatrix_10 (.col0(graph_1_level_5));
  DotMatrix #(.matrixcols(1), .matrixrows(16)) dotmatrix_11 (.col0(graph_1_level_8));
  DotMatrix #(.matrixcols(1), .matrixrows(16)) dotmatrix_12 (.col0(graph_1_level_14));
  DotMatrix #(.matrixcols(1), .matrixrows(16)) dotmatrix_13 (.col0(graph_1_level_12));
  DotMatrix #(.matrixcols(1), .matrixrows(16)) dotmatrix_14 (.col0(graph_1_level_16));
  DotMatrix #(.matrixcols(1), .matrixrows(16)) dotmatrix_15 (.col0(graph_1_level_13));
  DotMatrix #(.matrixcols(1), .matrixrows(16)) dotmatrix_16 (.col0(graph_1_level_15));
  DotMatrix #(.matrixcols(1), .matrixrows(16)) dotmatrix_17 (.col0(graph_1_level_17));

  // Notes on the sheet:
  //   HEXADECIMAL
  //   REPRESENTATION 3
  //   REPRESENTATION 1
  //   Ctl+1: Manipulate buttons
  //   Ctl+K: Start/stop the clocks
  //   Ctl+R: Reset the simulator
  //   Ctl+2: Move/edit wires and circuit components
  //   May need to close/reopen the simulator occasionally
  //   Menu: Simulate->Tick Freq->128Hz suggested freq
endmodule

module BCD11 (
  input  [7:0] D8_IN,
  output [11:0] D8_OUT
);

  ROM #(.dataWidth(12)) rom_1 (.addr(D8_IN), .data(D8_OUT));  // open: sel

  // Notes on the sheet:
  //   contents of rom_1 (hex, n*v repeats v):
  //   998 992 984 977 969 961 953 945 938 930 922 914 906 898 891 883 875 867 859 852 844 836 828 820 812
  //   805 797 789 781 773 766 758 750 742 734 727 719 711 703 695 688 680 672 664 656 648 641 633 625 617
  //   609 602 594 586 578 570 562 555 547 539 531 523 516 508 500 492 484 477 469 461 453 445 438 430 422
  //   414 406 398 391 383 375 367 359 352 344 336 328 320 312 305 297 289 281 273 266 258 250 242 234 227
  //   219 211 203 195 188 180 172 164 156 148 141 133 125 117 109 102 94 86 78 70 62 55 47 39 31 23 16 8 0
  //   8 16 23 31 39 47 55 62 70 78 86 94 102 109 117 125 133 141 148 156 164 172 180 188 195 203 211 219
  //   227 234 242 250 258 266 273 281 289 297 305 312 320 328 336 344 352 359 367 375 383 391 398 406 414
  //   422 430 438 445 453 461 469 477 484 492 500 508 516 523 531 539 547 555 562 570 578 586 594 602 609
  //   617 625 633 641 648 656 664 672 680 688 695 703 711 719 727 734 742 750 758 766 773 781 789 797 805
  //   812 820 828 836 844 852 859 867 875 883 891 898 906 914 922 930 938 945 953 961 969 977 984 992
endmodule

module BCD01 (
  input  [7:0] D8_IN,
  output [11:0] D8_OUT
);

  ROM #(.dataWidth(12)) rom_1 (.addr(D8_IN), .data(D8_OUT));  // open: sel

  // Notes on the sheet:
  //   contents of rom_1 (hex, n*v repeats v):
  //   0 4 8 12 16 20 23 27 31 35 39 43 47 51 55 59 62 66 70 74 78 82 86 90 94 98 102 105 109 113 117 121
  //   125 129 133 137 141 145 148 152 156 160 164 168 172 176 180 184 188 191 195 199 203 207 211 215 219
  //   223 227 230 234 238 242 246 250 254 258 262 266 270 273 277 281 285 289 293 297 301 305 309 312 316
  //   320 324 328 332 336 340 344 348 352 355 359 363 367 371 375 379 383 387 391 395 398 402 406 410 414
  //   418 422 426 430 434 438 441 445 449 453 457 461 465 469 473 477 480 484 488 492 496 500 504 508 512
  //   516 520 523 527 531 535 539 543 547 551 555 559 562 566 570 574 578 582 586 590 594 598 602 605 609
  //   613 617 621 625 629 633 637 641 645 648 652 656 660 664 668 672 676 680 684 688 691 695 699 703 707
  //   711 715 719 723 727 730 734 738 742 746 750 754 758 762 766 770 773 777 781 785 789 793 797 801 805
  //   809 812 816 820 824 828 832 836 840 844 848 852 855 859 863 867 871 875 879 883 887 891 895 898 902
  //   906 910 914 918 922 926 930 934 938 941 945 949 953 957 961 965 969 973 977 980 984 988 992 996
endmodule

// DLKDIV
module CLKDIV8 (
  input  CLK,
  input  [2:0] DIV3,
  output CLK_OUT
);

  wire [7:0] counter_1_q;

  Counter counter_1 (.Q(counter_1_q), .clk(CLK));  // open: load, D, count, carry, clr
  Multiplexer #(.select(3)) multiplexer_1 (
    .in0(counter_1_q[0]), .in1(counter_1_q[1]), .in2(counter_1_q[2]), .in3(counter_1_q[3]),
    .in4(counter_1_q[4]), .in5(counter_1_q[5]), .in6(counter_1_q[6]), .in7(counter_1_q[7]), .out(CLK_OUT),
    .sel(DIV3));  // open: en
endmodule

// DISPH
module display_hex (
  input  [7:0] D8_IN,
  output [3:0] LOHEX,
  output [3:0] HIHEX,
  output [15:0] LEVEL
);

  wire [15:0] shifter_1_out;

  Shifter #(.width(32)) shifter_1 (.in(32'hffff), .\dist ({1'b0, D8_IN[7:4]}), .out({LEVEL, shifter_1_out}));

  assign HIHEX = D8_IN[7:4];
  assign LOHEX = D8_IN[3:0];
endmodule

// DISP11
module display_11 (
  input  [7:0] D8_IN,
  output [15:0] LEVEL,
  output SIGN,
  output [3:0] ZERO,
  output DOT,
  output [3:0] TENTH,
  output [3:0] HNDRTH,
  output [3:0] THOUSNTH
);

  wire [15:0] shifter_1_out;

  Comparator #(.mode("unsigned")) comparator_1 (.a(D8_IN), .b(8'h80), .lt(SIGN));  // open: gt, eq
  BCD11 bcd11_1 (.D8_IN(D8_IN), .D8_OUT({TENTH, HNDRTH, THOUSNTH}));
  Shifter #(.width(32)) shifter_1 (.in(32'h8000), .\dist ({1'b0, D8_IN[7:4]}), .out({LEVEL, shifter_1_out}));

  assign DOT = 1'b1;
  assign ZERO = 4'b0000;
endmodule

// DISP01
module display_01 (
  input  [7:0] D8_IN,
  output [15:0] LEVEL,
  output [3:0] ZERO,
  output DOT,
  output [3:0] TENTH,
  output [3:0] HNDRTH,
  output [3:0] THOUSNTH
);

  wire [15:0] shifter_1_out;

  Shifter #(.width(32)) shifter_1 (.in(32'hffff), .\dist ({1'b0, D8_IN[7:4]}), .out({LEVEL, shifter_1_out}));
  BCD01 bcd01_1 (.D8_IN(D8_IN), .D8_OUT({TENTH, HNDRTH, THOUSNTH}));

  assign DOT = 1'b1;
  assign ZERO = 4'b0000;
endmodule

module GRAPH (
  input  [15:0] LEVEL,
  input  CLK,
  output [15:0] LEVEL_2,
  output [15:0] LEVEL_3,
  output [15:0] LEVEL_4,
  output [15:0] LEVEL_5,
  output [15:0] LEVEL_6,
  output [15:0] LEVEL_7,
  output [15:0] LEVEL_8,
  output [15:0] LEVEL_9,
  output [15:0] LEVEL_10,
  output [15:0] LEVEL_11,
  output [15:0] LEVEL_12,
  output [15:0] LEVEL_13,
  output [15:0] LEVEL_14,
  output [15:0] LEVEL_15,
  output [15:0] LEVEL_16,
  output [15:0] LEVEL_17
);

  Shift_Register #(.width(16), .length(16)) shift_register_1 (
    .in(LEVEL), .clk(CLK), .q0(LEVEL_17), .q1(LEVEL_16), .q2(LEVEL_15), .q3(LEVEL_14), .q4(LEVEL_13),
    .q5(LEVEL_12), .q6(LEVEL_11), .q7(LEVEL_10), .q8(LEVEL_9), .q9(LEVEL_8), .q10(LEVEL_7), .q11(LEVEL_6),
    .q12(LEVEL_5), .q13(LEVEL_4), .q14(LEVEL_3), .q15(LEVEL_2));  // open: shift, out, load, clr, d0, d1, d2, d3, d4, d5, d6, d7, d8, d9, d10, d11, d12, d13, d14, d15
endmodule

// VAR
module VAR8 (
  input  INC,
  input  DEC,
  output [7:0] COUNT8_OUT
);

  wire and_1_out, clock_1_out, not_1_out, or_1_out;

  not not_1 (not_1_out, INC);
  and and_1 (and_1_out, not_1_out, DEC);
  or or_1 (or_1_out, INC, DEC);
  Clock clock_1 (.out(clock_1_out));
  Counter #(.ongoal("stay")) counter_1 (
    .load(and_1_out), .count(or_1_out), .Q(COUNT8_OUT), .clk(clock_1_out));  // open: D, carry, clr

  // Notes on the sheet:
  //   INC=DEC, PAUSE
endmodule
