// Logisim project 06_signed_arithmetic.circ as structural Verilog: 18 circuits, main circuit main
module main (
);

  wire avg2_1_s1_avg, button_1_out, button_2_out, button_3_out, button_4_out, clkdiv8_1_clk_out, clock_1_out,
       display_11_1_dot, display_11_1_sign, display_11_2_dot, display_11_2_sign, display_11_3_dot,
       display_11_3_sign, display_11_4_dot, display_11_4_sign, dsc_1_s1_out, dsc_2_s1_out, mul11_1_s1_prod;
  wire [3:0] display_11_1_hndrth, display_11_1_tenth, display_11_1_thousnth, display_11_1_zero,
       display_11_2_hndrth, display_11_2_tenth, display_11_2_thousnth, display_11_2_zero,
       display_11_3_hndrth, display_11_3_tenth, display_11_3_thousnth, display_11_3_zero,
       display_11_4_hndrth, display_11_4_tenth, display_11_4_thousnth, display_11_4_zero;
  wire [7:0] addie_1_d8_out, addie_1_d8_rng_out, addie_2_d8_out, d8rng_1_d8_rng_out, dsc_1_d8_rng_out,
       dsc_2_d8_rng_out, var8_1_count8_out, var8_2_count8_out;
  wire [15:0] display_11_4_level, graph_1_level_2, graph_1_level_3, graph_1_level_4, graph_1_level_5,
       graph_1_level_6, graph_1_level_7, graph_1_level_8, graph_1_level_9, graph_1_level_10,
       graph_1_level_11, graph_1_level_12, graph_1_level_13, graph_1_level_14, graph_1_level_15,
       graph_1_level_16, graph_1_level_17;

  Button button_1 (.out(button_1_out));
  Button button_2 (.out(button_2_out));
  VAR8 var8_1 (.INC(button_1_out), .DEC(button_2_out), .COUNT8_OUT(var8_1_count8_out));
  D8RNG d8rng_1 (.D8_RNG_OUT(d8rng_1_d8_rng_out));
  display_11 display_11_1 (
    .D8_IN(var8_1_count8_out), .SIGN(display_11_1_sign), .ZERO(display_11_1_zero), .DOT(display_11_1_dot),
    .TENTH(display_11_1_tenth), .HNDRTH(display_11_1_hndrth), .THOUSNTH(display_11_1_thousnth));  // open: LEVEL
  DSC dsc_1 (
    .D8_RNG_IN(d8rng_1_d8_rng_out), .D8_IN(var8_1_count8_out), .D8_RNG_OUT(dsc_1_d8_rng_out),
    .S1_OUT(dsc_1_s1_out));
  _7_Segment_Display u_7_segment_display_1 (.g(display_11_1_sign));  // open: f, a, b, e, d, c, dp
  Hex_Digit_Display hex_digit_display_1 (.value(display_11_1_tenth));  // open: dp
  Hex_Digit_Display hex_digit_display_2 (.value(display_11_1_zero), .dp(display_11_1_dot));
  Hex_Digit_Display hex_digit_display_3 (.value(display_11_1_hndrth));  // open: dp
  Hex_Digit_Display hex_digit_display_4 (.value(display_11_1_thousnth));  // open: dp
  AVG2 avg2_1 (.S1_A(dsc_1_s1_out), .S1_B(dsc_2_s1_out), .S1_AVG(avg2_1_s1_avg));
  MUL11 mul11_1 (.S1_A(dsc_1_s1_out), .S1_B(dsc_2_s1_out), .S1_PROD(mul11_1_s1_prod));
  Button button_3 (.out(button_3_out));
  Button button_4 (.out(button_4_out));
  VAR8 var8_2 (.INC(button_3_out), .DEC(button_4_out), .COUNT8_OUT(var8_2_count8_out));
  DSC dsc_2 (
    .D8_RNG_IN(dsc_1_d8_rng_out), .D8_IN(var8_2_count8_out), .D8_RNG_OUT(dsc_2_d8_rng_out),
    .S1_OUT(dsc_2_s1_out));
  ADDIE addie_1 (
    .D8_RNG(dsc_2_d8_rng_out), .S1_IN(avg2_1_s1_avg), .D8_RNG_OUT(addie_1_d8_rng_out), .D8_OUT(addie_1_d8_out));  // open: S1_OUT
  ADDIE addie_2 (
    .D8_RNG(addie_1_d8_rng_out), .S1_IN(mul11_1_s1_prod), .D8_OUT(addie_2_d8_out));  // open: D8_RNG_OUT, S1_OUT
  display_11 display_11_2 (
    .D8_IN(var8_2_count8_out), .SIGN(display_11_2_sign), .ZERO(display_11_2_zero), .DOT(display_11_2_dot),
    .TENTH(display_11_2_tenth), .HNDRTH(display_11_2_hndrth), .THOUSNTH(display_11_2_thousnth));  // open: LEVEL
  display_11 display_11_3 (
    .D8_IN(addie_1_d8_out), .SIGN(display_11_3_sign), .ZERO(display_11_3_zero), .DOT(display_11_3_dot),
    .TENTH(display_11_3_tenth), .HNDRTH(display_11_3_hndrth), .THOUSNTH(display_11_3_thousnth));  // open: LEVEL
  display_11 display_11_4 (
    .D8_IN(addie_2_d8_out), .LEVEL(display_11_4_level), .SIGN(display_11_4_sign), .ZERO(display_11_4_zero),
    .DOT(display_11_4_dot), .TENTH(display_11_4_tenth), .HNDRTH(display_11_4_hndrth),
    .THOUSNTH(display_11_4_thousnth));
  _7_Segment_Display u_7_segment_display_2 (.g(display_11_2_sign));  // open: f, a, b, e, d, c, dp
  Hex_Digit_Display hex_digit_display_5 (.value(display_11_2_zero), .dp(display_11_2_dot));
  _7_Segment_Display u_7_segment_display_3 (.g(display_11_3_sign));  // open: f, a, b, e, d, c, dp
  Hex_Digit_Display hex_digit_display_6 (.value(display_11_3_zero), .dp(display_11_3_dot));
  _7_Segment_Display u_7_segment_display_4 (.g(display_11_4_sign));  // open: f, a, b, e, d, c, dp
  Hex_Digit_Display hex_digit_display_7 (.value(display_11_4_zero), .dp(display_11_4_dot));
  Hex_Digit_Display hex_digit_display_8 (.value(display_11_2_tenth));  // open: dp
  Hex_Digit_Display hex_digit_display_9 (.value(display_11_3_tenth));  // open: dp
  Hex_Digit_Display hex_digit_display_10 (.value(display_11_4_tenth));  // open: dp
  Hex_Digit_Display hex_digit_display_11 (.value(display_11_2_thousnth));  // open: dp
  Hex_Digit_Display hex_digit_display_12 (.value(display_11_2_hndrth));  // open: dp
  Hex_Digit_Display hex_digit_display_13 (.value(display_11_3_thousnth));  // open: dp
  Hex_Digit_Display hex_digit_display_14 (.value(display_11_3_hndrth));  // open: dp
  Hex_Digit_Display hex_digit_display_15 (.value(display_11_4_thousnth));  // open: dp
  Hex_Digit_Display hex_digit_display_16 (.value(display_11_4_hndrth));  // open: dp
  Clock clock_1 (.out(clock_1_out));
  DotMatrix #(.matrixcols(1), .matrixrows(16)) dotmatrix_1 (.col0(graph_1_level_2));
  DotMatrix #(.matrixcols(1), .matrixrows(16)) dotmatrix_2 (.col0(graph_1_level_5));
  DotMatrix #(.matrixcols(1), .matrixrows(16)) dotmatrix_3 (.col0(graph_1_level_3));
  DotMatrix #(.matrixcols(1), .matrixrows(16)) dotmatrix_4 (.col0(graph_1_level_4));
  GRAPH graph_1 (
    .LEVEL(display_11_4_level), .CLK(clkdiv8_1_clk_out), .LEVEL_2(graph_1_level_2),
    .LEVEL_3(graph_1_level_3), .LEVEL_4(graph_1_level_4), .LEVEL_5(graph_1_level_5),
    .LEVEL_6(graph_1_level_6), .LEVEL_7(graph_1_level_7), .LEVEL_8(graph_1_level_8),
    .LEVEL_9(graph_1_level_9), .LEVEL_10(graph_1_level_10), .LEVEL_11(graph_1_level_11),
    .LEVEL_12(graph_1_level_12), .LEVEL_13(graph_1_level_13), .LEVEL_14(graph_1_level_14),
    .LEVEL_15(graph_1_level_15), .LEVEL_16(graph_1_level_16), .LEVEL_17(graph_1_level_17));
  CLKDIV8 clkdiv8_1 (.CLK(clock_1_out), .DIV3(3'b100), .CLK_OUT(clkdiv8_1_clk_out));
  DotMatrix #(.matrixcols(1), .matrixrows(16)) dotmatrix_5 (.col0(graph_1_level_8));
  DotMatrix #(.matrixcols(1), .matrixrows(16)) dotmatrix_6 (.col0(graph_1_level_10));
  DotMatrix #(.matrixcols(1), .matrixrows(16)) dotmatrix_7 (.col0(graph_1_level_13));
  DotMatrix #(.matrixcols(1), .matrixrows(16)) dotmatrix_8 (.col0(graph_1_level_6));
  DotMatrix #(.matrixcols(1), .matrixrows(16)) dotmatrix_9 (.col0(graph_1_level_7));
  DotMatrix #(.matrixcols(1), .matrixrows(16)) dotmatrix_10 (.col0(graph_1_level_9));
  DotMatrix #(.matrixcols(1), .matrixrows(16)) dotmatrix_11 (.col0(graph_1_level_11));
  DotMatrix #(.matrixcols(1), .matrixrows(16)) dotmatrix_12 (.col0(graph_1_level_12));
  DotMatrix #(.matrixcols(1), .matrixrows(16)) dotmatrix_13 (.col0(graph_1_level_15));
  DotMatrix #(.matrixcols(1), .matrixrows(16)) dotmatrix_14 (.col0(graph_1_level_16));
  DotMatrix #(.matrixcols(1), .matrixrows(16)) dotmatrix_15 (.col0(graph_1_level_14));
  DotMatrix #(.matrixcols(1), .matrixrows(16)) dotmatrix_16 (.col0(graph_1_level_17));

  // Notes on the sheet:
  //   Menu: Simulate->Tick Freq->128Hz suggested freq
  //   A
  //   B
  //   (A+B)/2
  //   A x B
endmodule

module ADDIE (
  input  [7:0] D8_RNG,
  input  S1_IN,
  output [7:0] D8_RNG_OUT,
  output S1_OUT,
  output [7:0] D8_OUT
);

  wire not_1_out;

  not not_1 (not_1_out, S1_OUT);
  INT int_1 (
    .D8_RNG_IN(D8_RNG), .S1_A(not_1_out), .S1_B(S1_IN), .D8_RNG_OUT(D8_RNG_OUT), .S1_OUT(S1_OUT),
    .D8_OUT(D8_OUT));
endmodule

module AVG2 (
  input  S1_A,
  input  S1_B,
  output S1_AVG
);

  wire clock_1_out, t_ff_1_qn;

  Clock clock_1 (.out(clock_1_out));
  Multiplexer #(.enable("false")) multiplexer_1 (.in0(S1_A), .in1(S1_B), .out(S1_AVG), .sel(t_ff_1_qn));
  T_Flip_Flop t_ff_1 (.clk(clock_1_out), .T(1'b1), .Qn(t_ff_1_qn));  // open: Q, preset, reset, en
endmodule

module BCD01 (
  input  [7:0] D8_IN,
  output [11:0] D8_OUT
);

  ROM #(.dataWidth(12)) rom_1 (.addr(D8_IN), .data(D8_OUT));  // open: sel

  // Notes on the sheet:
  //   contents of rom_1 (hex, n*v repeats v):
  //   0 4 8 12 16 20 23 27 31 35 39 43 47 51 55 59 62 66 70 74 78 82 86 90 94 98 102 105 109 113 117 121
  //   125 129 133 137 141 145 148 152 156 160 164 168 172 176 180 184 188 191 195 199 203 207 211 215 219
  //   223 227 230 234 238 242 246 250 254 258 262 266 270 273 277 281 285 289 293 297 301 305 309 312 316
  //   320 324 328 332 336 340 344 348 352 355 359 363 367 371 375 379 383 387 391 395 398 402 406 410 414
  //   418 422 426 430 434 438 441 445 449 453 457 461 465 469 473 477 480 484 488 492 496 500 504 508 512
  //   516 520 523 527 531 535 539 543 547 551 555 559 562 566 570 574 578 582 586 590 594 598 602 605 609
  //   613 617 621 625 629 633 637 641 645 648 652 656 660 664 668 672 676 680 684 688 691 695 699 703 707
  //   711 715 719 723 727 730 734 738 742 746 750 754 758 762 766 770 773 777 781 785 789 793 797 801 805
  //   809 812 816 820 824 828 832 836 840 844 848 852 855 859 863 867 871 875 879 883 887 891 895 898 902
  //   906 910 914 918 922 926 930 934 938 941 945 949 953 957 961 965 969 973 977 980 984 988 992 996
endmodule

module BCD11 (
  input  [7:0] D8_IN,
  output [11:0] D8_OUT
);

  ROM #(.dataWidth(12)) rom_1 (.addr(D8_IN), .data(D8_OUT));  // open: sel

  // Notes on the sheet:
  //   contents of rom_1 (hex, n*v repeats v):
  //   998 992 984 977 969 961 953 945 938 930 922 914 906 898 891 883 875 867 859 852 844 836 828 820 812
  //   805 797 789 781 773 766 758 750 742 734 727 719 711 703 695 688 680 672 664 656 648 641 633 625 617
  //   609 602 594 586 578 570 562 555 547 539 531 523 516 508 500 492 484 477 469 461 453 445 438 430 422
  //   414 406 398 391 383 375 367 359 352 344 336 328 320 312 305 297 289 281 273 266 258 250 242 234 227
  //   219 211 203 195 188 180 172 164 156 148 141 133 125 117 109 102 94 86 78 70 62 55 47 39 31 23 16 8 0
  //   8 16 23 31 39 47 55 62 70 78 86 94 102 109 117 125 133 141 148 156 164 172 180 188 195 203 211 219
  //   227 234 242 250 258 266 273 281 289 297 305 312 320 328 336 344 352 359 367 375 383 391 398 406 414
  //   422 430 438 445 453 461 469 477 484 492 500 508 516 523 531 539 547 555 562 570 578 586 594 602 609
  //   617 625 633 641 648 656 664 672 680 688 695 703 711 719 727 734 742 750 758 766 773 781 789 797 805
  //   812 820 828 836 844 852 859 867 875 883 891 898 906 914 922 930 938 945 953 961 969 977 984 992
endmodule

// DLKDIV
module CLKDIV8 (
  input  CLK,
  input  [2:0] DIV3,
  output CLK_OUT
);

  wire [7:0] counter_1_q;

  Counter counter_1 (.Q(counter_1_q), .clk(CLK));  // open: load, D, count, carry, clr
  Multiplexer #(.select(3)) multiplexer_1 (
    .in0(counter_1_q[0]), .in1(counter_1_q[1]), .in2(counter_1_q[2]), .in3(counter_1_q[3]),
    .in4(counter_1_q[4]), .in5(counter_1_q[5]), .in6(counter_1_q[6]), .in7(counter_1_q[7]), .out(CLK_OUT),
    .sel(DIV3));  // open: en
endmodule

module D8RNG (
  output [7:0] D8_RNG_OUT
);

  wire clock_1_out;

  Clock clock_1 (.out(clock_1_out));
  Random random_1 (.clk(clock_1_out), .out(D8_RNG_OUT));  // open: next, clr
endmodule

module DSC (
  input  [7:0] D8_RNG_IN,
  input  [7:0] D8_IN,
  output [7:0] D8_RNG_OUT,
  output S1_OUT
);

  wire comparator_1_eq, comparator_1_lt;

  SBOX sbox_1 (.D8_IN(D8_RNG_IN), .D8_OUT(D8_RNG_OUT));
  Comparator #(.mode("unsigned")) comparator_1 (
    .a(D8_RNG_IN), .b(D8_IN), .eq(comparator_1_eq), .lt(comparator_1_lt));  // open: gt
  or or_1 (S1_OUT, comparator_1_eq, comparator_1_lt);
endmodule

// DISPH
module display_hex (
  input  [7:0] D8_IN,
  output [3:0] LOHEX,
  output [3:0] HIHEX,
  output [15:0] LEVEL
);

  wire [15:0] shifter_1_out;

  Shifter #(.width(32)) shifter_1 (.in(32'hffff), .\dist ({1'b0, D8_IN[7:4]}), .out({LEVEL, shifter_1_out}));

  assign HIHEX = D8_IN[7:4];
  assign LOHEX = D8_IN[3:0];
endmodule

// DISP01
module display_01 (
  input  [7:0] D8_IN,
  output [15:0] LEVEL,
  output [3:0] ZERO,
  output DOT,
  output [3:0] TENTH,
  output [3:0] HNDRTH,
  output [3:0] THOUSNTH
);

  wire [15:0] shifter_1_out;

  Shifter #(.width(32)) shifter_1 (.in(32'h10000), .\dist ({1'b0, D8_IN[7:4]}), .out({LEVEL, shifter_1_out}));
  BCD01 bcd01_1 (.D8_IN(D8_IN), .D8_OUT({TENTH, HNDRTH, THOUSNTH}));

  assign DOT = 1'b1;
  assign ZERO = 4'b0000;
endmodule

// DISP11
module display_11 (
  input  [7:0] D8_IN,
  output [15:0] LEVEL,
  output SIGN,
  output [3:0] ZERO,
  output DOT,
  output [3:0] TENTH,
  output [3:0] HNDRTH,
  output [3:0] THOUSNTH
);

  wire [15:0] shifter_1_out;

  Comparator #(.mode("unsigned")) comparator_1 (.a(D8_IN), .b(8'h80), .lt(SIGN));  // open: gt, eq
  BCD11 bcd11_1 (.D8_IN(D8_IN), .D8_OUT({TENTH, HNDRTH, THOUSNTH}));
  Shifter #(.width(32)) shifter_1 (.in(32'h10000), .\dist ({1'b0, D8_IN[7:4]}), .out({LEVEL, shifter_1_out}));

  assign DOT = 1'b1;
  assign ZERO = 4'b0000;
endmodule

module GRAPH (
  input  [15:0] LEVEL,
  input  CLK,
  output [15:0] LEVEL_2,
  output [15:0] LEVEL_3,
  output [15:0] LEVEL_4,
  output [15:0] LEVEL_5,
  output [15:0] LEVEL_6,
  output [15:0] LEVEL_7,
  output [15:0] LEVEL_8,
  output [15:0] LEVEL_9,
  output [15:0] LEVEL_10,
  output [15:0] LEVEL_11,
  output [15:0] LEVEL_12,
  output [15:0] LEVEL_13,
  output [15:0] LEVEL_14,
  output [15:0] LEVEL_15,
  output [15:0] LEVEL_16,
  output [15:0] LEVEL_17
);

  Shift_Register #(.width(16), .length(16)) shift_register_1 (
    .in(LEVEL), .clk(CLK), .q0(LEVEL_17), .q1(LEVEL_16), .q2(LEVEL_15), .q3(LEVEL_14), .q4(LEVEL_13),
    .q5(LEVEL_12), .q6(LEVEL_11), .q7(LEVEL_10), .q8(LEVEL_9), .q9(LEVEL_8), .q10(LEVEL_7), .q11(LEVEL_6),
    .q12(LEVEL_5), .q13(LEVEL_4), .q14(LEVEL_3), .q15(LEVEL_2));  // open: shift, out, load, clr, d0, d1, d2, d3, d4, d5, d6, d7, d8, d9, d10, d11, d12, d13, d14, d15
endmodule

module INT (
  input  [7:0] D8_RNG_IN,
  input  S1_A,
  input  S1_B,
  output [7:0] D8_RNG_OUT,
  output S1_OUT,
  output [7:0] D8_OUT
);

  wire and_1_out, clock_1_out, not_1_out, not_2_out, xnor_1_out;

  not not_1 (not_1_out, S1_A);
  and and_1 (and_1_out, not_1_out, not_2_out);
  not not_2 (not_2_out, S1_B);
  xnor xnor_1 (xnor_1_out, S1_A, S1_B);
  Clock clock_1 (.out(clock_1_out));
  DSC dsc_1 (.D8_RNG_IN(D8_RNG_IN), .D8_IN(D8_OUT), .D8_RNG_OUT(D8_RNG_OUT), .S1_OUT(S1_OUT));
  Counter #(.ongoal("stay")) counter_1 (
    .load(and_1_out), .count(xnor_1_out), .Q(D8_OUT), .clk(clock_1_out));  // open: D, carry, clr

  // Notes on the sheet:
  //   A=1, B=1, INC
  //   A-0, B=0, DEC
  //   ELSE PAUSE
endmodule

module MUL01 (
  input  S1_A,
  input  S1_B,
  output S1_PROD
);

  and and_1 (S1_PROD, S1_A, S1_B);
endmodule

module MUL11 (
  input  S1_A,
  input  S1_B,
  output S1_PROD
);

  wire nand_1_out, nand_2_out, not_1_out, not_2_out;

  not not_1 (not_1_out, S1_A);
  not not_2 (not_2_out, S1_B);
  nand nand_1 (nand_1_out, S1_A, S1_B);
  nand nand_2 (nand_2_out, not_1_out, not_2_out);
  nand nand_3 (S1_PROD, nand_1_out, nand_2_out);
endmodule

module SBOX (
  input  [7:0] D8_IN,
  output [7:0] D8_OUT
);

  ROM rom_1 (.addr(D8_IN), .data(D8_OUT));  // open: sel

  // Notes on the sheet:
  //   8-bit SBOX from Pearson's hash
  //   contents of rom_1 (hex, n*v repeats v):
  //   1 57 31 c b0 b2 66 a6 79 c1 6 54 f9 e6 2c a3 e c5 d5 b5 a1 55 da 50 40 ef 18 e2 ec 8e 26 c8 6e b1 68
  //   67 8d fd ff 32 4d 65 51 12 2d 60 1f de 19 6b be 46 56 ed f0 22 48 f2 14 d6 f4 e3 95 eb 61 ea 39 16
  //   3c fa 52 af d0 5 7f c7 6f 3e 87 f8 ae a9 d3 3a 42 9a 6a c3 f5 ab 11 bb b6 b3 0 f3 84 38 94 4b 80 85
  //   9e 64 82 7e 5b d 99 f6 d8 db 77 44 df 4e 53 58 c9 63 7a b 5c 20 88 72 34 a 8a 1e 30 b7 9c 23 3d 1a
  //   8f 4a fb 5e 81 a2 3f 98 aa 7 73 a7 f1 ce 3 96 37 3b 97 dc 5a 35 17 83 7d ad f ee 4f 5f 59 10 69 89
  //   e1 e0 d9 a0 25 7b 76 49 2 9d 2e 74 9 91 86 e4 cf d4 ca d7 45 e5 1b bc 43 7c a8 fc 2a 4 1d 6c 15 f7
  //   13 cd 27 cb e9 28 ba 93 c6 c0 9b 21 a4 bf 62 cc a5 b4 75 4c 8c 24 d2 ac 29 36 9f 8 b9 e8 71 c4 e7 2f
  //   92 78 33 41 1c 90 fe dd 5d bd c2 8b 70 2b 47 6d b8 d1
endmodule

module SCOUNT (
  input  [7:0] D8_RNG,
  input  S1_INC,
  input  S1_DEC,
  output [7:0] D8_RNG_OUT,
  output S1_OUT,
  output [7:0] D8_OUT
);

  wire and_1_out, clock_1_out, not_1_out, xor_1_out;

  not not_1 (not_1_out, S1_INC);
  and and_1 (and_1_out, not_1_out, S1_DEC);
  xor xor_1 (xor_1_out, S1_INC, S1_DEC);
  Clock clock_1 (.out(clock_1_out));
  Counter #(.ongoal("stay")) counter_1 (
    .load(and_1_out), .count(xor_1_out), .Q(D8_OUT), .clk(clock_1_out));  // open: D, carry, clr
  DSC dsc_1 (.D8_RNG_IN(D8_RNG), .D8_IN(D8_OUT), .D8_RNG_OUT(D8_RNG_OUT), .S1_OUT(S1_OUT));

  // Notes on the sheet:
  //   INC=DEC, PAUSE
endmodule

module VAR8 (
  input  INC,
  input  DEC,
  output [7:0] COUNT8_OUT
);

  wire and_1_out, clock_1_out, not_1_out, or_1_out;

  not not_1 (not_1_out, INC);
  and and_1 (and_1_out, not_1_out, DEC);
  or or_1 (or_1_out, INC, DEC);
  Clock clock_1 (.out(clock_1_out));
  Counter #(.ongoal("stay")) counter_1 (
    .load(and_1_out), .count(or_1_out), .Q(COUNT8_OUT), .clk(clock_1_out));  // open: D, carry, clr

  // Notes on the sheet:
  //   INC=DEC, PAUSE
endmodule
